# Fritzing sketch Arduino_Uno_Midi (saved by Fritzing 1.0.1rc)
breadboards: 1

parts:
  Bauteil1 = Arduino Uno (Rev3)
  IC1 = IC, DIP package, 8 pins [chip_label=6N137]
  U1 = MIDI_CONN_FEMALE_SUPPORT [package=din_5_female_support]
  part = Ceramic Capacitor [capacitance=100nF voltage=35V package="100 mil [THT, multilayer]"]
  part_2 = Resistor [tolerance=±5% power=0.25W resistance=4.7k package=THT]
  part_3 = Resistor [tolerance=±5% power=0.25W resistance=1k package=THT]
  part_4 = Rectifier Diode [part_number=1N4148 package="Melf DO-213 AB [SMD]"]
  part_5 = Resistor [tolerance=±5% power=0.25W resistance=220 package=THT]

nets:
  N1: Bauteil1.GND, IC1.pin5, part.0
  N2: Bauteil1.D2, IC1.pin6, part_3.Pin_1
  N3: Bauteil1.5V, IC1.pin8, part.1, part_2.Pin_0
  N4: IC1.pin2, part_4.cathode, part_5.Pin_0
  N5: IC1.pin3, U1.MIDI_IN, part_4.anode
  N6: U1.MIDI_OUT, part_5.Pin_1
  N7: part_2.Pin_1, part_3.Pin_0
